# Fritzing sketch zevehicle (saved by Fritzing 0.9.9b)
breadboards: 1

parts:
  IC1 = H-Bridge [package=THT]
  Arduino = Arduino Uno (Rev3)
  M1 = gear-motor
  IR1 = TSOP312.., 314.. [package=THT]
  M2 = gear-motor

nets:
  N1: IC1.1_2EN, Arduino.D4
  N2: IC1.1A, Arduino.D5_PWM
  N3: IC1.1Y, M2.pin_1
  GND: IC1.GND1, IC1.GND2, IC1.GND3, IC1.GND4, Arduino.GND, IR1.GND
  N4: IC1.2Y, M2.pin_2
  N5: IC1.2A, Arduino.D6_PWM
  5V: IC1.VCC2, IC1.VCC1, Arduino.5V, IR1.Vs
  N6: IC1.3_4EN, Arduino.D8
  N7: IC1.3A, Arduino.D9_PWM
  N8: IC1.3Y, M1.pin_2
  N9: IC1.4Y, M1.pin_1
  N10: IC1.4A, Arduino.D10_PWM/SS
  N11: Arduino.D2, IR1.Data
