# Fritzing sketch zevehicle2 (saved by Fritzing 0.9.9b)
breadboards: 1

parts:
  IC1 = H-Bridge [package=THT]
  IR1 = TSOP312.., 314.. [package=THT]
  Arduino = Arduino Uno (Rev3)
  IC2 = H-Bridge [package=THT]
  M1 = Stepper Motor - Bipolar
  M2 = Stepper Motor - Bipolar
  M3 = MAX7219 8x8 single Led Matrix Module

nets:
  N1: IC1.1_2EN, IC1.3_4EN, Arduino.D3_PWM, IC2.1_2EN, IC2.3_4EN
  N2: IC1.1A, Arduino.D10_PWM/SS
  M2A: IC1.1Y, M2.A
  GND: IC1.GND1, IC1.GND2, IC1.GND3, IC1.GND4, IR1.GND, Arduino.GND, IC2.GND1, IC2.GND2, IC2.GND3, IC2.GND4, M3.I-GND-1, M3.O-GND-1, M3.I-GND-2, M3.O-GND-2, M3.I-GND-3, M3.O-GND-3, M3.I-GND-4
  M2B: IC1.2Y, M2.B
  N3: IC1.2A, Arduino.D11_PWM/MOSI
  7V: IC1.VCC2, Arduino.VIN, IC2.VCC2, M3.I-VCC-1, M3.O-VCC-1, M3.I-VCC-2, M3.O-VCC-2, M3.I-VCC-3, M3.O-VCC-3, M3.I-VCC-4
  N4: IC1.3A, Arduino.D8
  M2C: IC1.3Y, M2.C
  M2D: IC1.4Y, M2.D
  N5: IC1.4A, Arduino.D9_PWM
  5V: IC1.VCC1, IR1.Vs, Arduino.5V, IC2.VCC1
  N6: IR1.Data, Arduino.D2
  N7: Arduino.A4/SDA, M3.I-CS-1, M3.O-CS-1, M3.I-CS-2, M3.O-CS-2, M3.I-CS-3, M3.O-CS-3, M3.I-CS-4
  N8: Arduino.A5/SCL, M3.I-CLK-1, M3.O-CLK-1, M3.I-CLK-2, M3.O-CLK-2, M3.I-CLK-3, M3.O-CLK-3, M3.I-CLK-4
  N9: Arduino.D12/MISO, M3.I-DIN-1
  N10: Arduino.D4, IC2.1A
  N11: Arduino.D5_PWM, IC2.2A
  N12: Arduino.D6_PWM, IC2.3A
  N13: Arduino.D7, IC2.4A
  M1A: IC2.1Y, M1.A
  M1B: IC2.2Y, M1.B
  M1C: IC2.3Y, M1.C
  M1D: IC2.4Y, M1.D
  N14: M3.O-DOUT-1, M3.I-DIN-2
  N15: M3.O-DOUT-2, M3.I-DIN-3
  N16: M3.O-DOUT-3, M3.I-DIN-4

custom parts:
  MAX7219 8x8 single Led Matrix Module: Description: MAX7219 8x8 LedMatrix single Red Module Dimensions: 32x32mm Documents:
