# Fritzing sketch zevehicle2_nano (saved by Fritzing 0.9.9b)
circuit board: 8.46667cm x 5.64444cm
breadboards: 1
stripboards: 1

parts:
  IC1 = H-Bridge [package=THT]
  IR1 = TSOP312.., 314.. [package=THT]
  IC2 = H-Bridge [package=THT]
  M1 = Stepper Motor - Bipolar
  M2 = Stepper Motor - Bipolar
  M3 = MAX7219 8x8 single Led Matrix Module
  Composant1 = Arduino Nano (Rev3.0)
  J1 = female pin header, 15 pins [form="♀ (female)"]
  J2 = female pin header, 15 pins [form="♀ (female)"]  # not connected
  J3 = female pin header, 8 pins [form="♀ (female)"]  # not connected
  J4 = female pin header, 8 pins [form="♀ (female)"]
  J5 = female pin header, 8 pins [form="♀ (female)"]  # not connected
  J6 = female pin header, 8 pins [form="♀ (female)"]
  J7 = female pin header, 4 pins [form="♀ (female)"]
  J8 = female pin header, 4 pins [form="♀ (female)"]
  J9 = female pin header, 4 pins [form="♀ (female)"]

nets:
  N1: IC1.1_2EN, IC1.3_4EN, IC2.1_2EN, IC2.3_4EN, Composant1.D3
  N2: IC1.1A, Composant1.D10
  M2A: IC1.1Y, M2.A
  GND: IC1.GND1, IC1.GND2, IC1.GND3, IC1.GND4, IR1.GND, IC2.GND1, IC2.GND2, IC2.GND3, IC2.GND4, M3.I-GND-1, M3.O-GND-1, M3.I-GND-2, M3.O-GND-2, M3.I-GND-3, M3.O-GND-3, M3.I-GND-4, Composant1.GND
  M2B: IC1.2Y, M2.B
  N3: IC1.2A, Composant1.D11/MOSI
  7V: IC1.VCC2, IC2.VCC2, M3.I-VCC-1, M3.O-VCC-1, M3.I-VCC-2, M3.O-VCC-2, M3.I-VCC-3, M3.O-VCC-3, M3.I-VCC-4, Composant1.VIN
  N4: IC1.3A, Composant1.D8
  M2C: IC1.3Y, M2.C
  M2D: IC1.4Y, M2.D
  N5: IC1.4A, Composant1.D9
  5V: IC1.VCC1, IR1.Vs, IC2.VCC1, Composant1.5V
  N6: IR1.Data, Composant1.D2
  N7: IC2.1A, Composant1.D4
  M1A: IC2.1Y, M1.A
  M1B: IC2.2Y, M1.B
  N8: IC2.2A, Composant1.D5
  N9: IC2.3A, Composant1.D6
  M1C: IC2.3Y, M1.C
  M1D: IC2.4Y, M1.D
  N10: IC2.4A, Composant1.D7
  N11: M3.I-CLK-1, M3.O-CLK-1, M3.I-CLK-2, M3.O-CLK-2, M3.I-CLK-3, M3.O-CLK-3, M3.I-CLK-4, Composant1.A5
  N12: M3.I-CS-1, M3.O-CS-1, M3.I-CS-2, M3.O-CS-2, M3.I-CS-3, M3.O-CS-3, M3.I-CS-4, Composant1.A4
  N13: M3.I-DIN-1, Composant1.A3
  N14: M3.O-DOUT-1, M3.I-DIN-2
  N15: M3.O-DOUT-2, M3.I-DIN-3
  N16: M3.O-DOUT-3, M3.I-DIN-4
  N17: J1.pin2, J9.pin1
  N18: J4.pin6, J7.pin2
  N19: J6.pin3, J8.pin4
  N20: J6.pin6, J8.pin2

custom parts:
  MAX7219 8x8 single Led Matrix Module: Description: MAX7219 8x8 LedMatrix single Red Module Dimensions: 32x32mm Documents:
