# Fritzing sketch zevehicle3 (saved by Fritzing 0.9.9b)

parts:
  Arduino = Arduino Uno (Rev3)
  M1 = Stepper Motor - Bipolar
  M2 = Stepper Motor - Bipolar
  Composant3 = DeuLigne 1.1 - The Snootlab's LCD shield for Arduino
  IC3 = H-Bridge [package=THT]
  IC4 = H-Bridge [package=THT]
  IR1 = TSOP312.., 314.. [package=THT]
  Composant4 = Arduino ProtoShield
  Composant2 = Arduino Prototyping Shield
  J1 = female pin header, 8 pins [form="♀ (female)"]
  J2 = female pin header, 8 pins [form="♀ (female)"]
  J3 = female pin header, 8 pins [form="♀ (female)"]
  J4 = female pin header, 8 pins [form="♀ (female)"]
  IC5 = H-Bridge [package=THT]  # not connected

nets:
  A0: Arduino.A0, Composant3.A0, Composant2.A0
  A1: Arduino.A1, Composant3.A1, IC4.2A, Composant2.A1, Composant2.N$318
  A2: Arduino.A2, Composant3.A2, IC4.1A, Composant2.A2, Composant2.N$309
  A3: Arduino.A3, Composant3.A3, IC4.4A, Composant2.A3, Composant2.N$399
  A4: Arduino.A4/SDA, Composant3.A4(SDA), IC4.3A, Composant2.A4, Composant2.N$380
  A5: Arduino.A5/SCL, Composant3.A5(CLK), Composant2.A5
  D8: Arduino.D8, Composant3.D8, Composant2.D8
  D9: Arduino.D9_PWM, Composant3.D9, Composant2.D9
  D10: Arduino.D10_PWM/SS, Composant3.D10_SS, Composant2.D10
  D11: Arduino.D11_PWM/MOSI, Composant3.D11_MOSI, IC3.1A, Composant2.D11, Composant2.N$281
  D12: Arduino.D12/MISO, Composant3.D12_MISO, IC3.4A, Composant2.D12, Composant2.N$273
  D13: Arduino.D13/SCK, Composant3.D13_SCK, IC3.3A, Composant2.D13, Composant2.N$231
  GND: Arduino.GND, Composant3.GND, IC3.GND1, IC3.GND2, IC3.GND3, IC3.GND4, IC4.GND1, IC4.GND2, IC4.GND3, IC4.GND4, IR1.GND, Composant2.GND, Composant2.N$43, Composant2.N$51, Composant2.N$252, Composant2.N$271, Composant2.N$321
  D0: Arduino.D0/RX, Composant3.D0_RX, Composant2.D0(RX)
  D1: Arduino.D1/TX, Composant3.D1_TX, Composant2.D1(TX)
  D2: Arduino.D2, Composant3.D2, IR1.Data, Composant2.D2, Composant2.N$325
  D3: Arduino.D3_PWM, Composant3.D3, IC3.2A, Composant2.D3, Composant2.N$237
  D4: Arduino.D4, Composant3.D4, Composant2.D4
  D5: Arduino.D5_PWM, Composant3.D5, Composant2.D5
  D6: Arduino.D6_PWM, Composant3.D6, Composant2.D6
  D7: Arduino.D7, Composant3.D7, Composant2.D7
  5V: Arduino.5V, Composant3.+5V, IC3.VCC1, IC4.VCC1, IR1.Vs, Composant2.+5V, Composant2.N$280, Composant2.N$322, Composant2.N$402
  7V: Arduino.VIN, Composant3.VIN, IC3.VCC2, IC4.VCC2, Composant2.+9V, Composant2.N$238, Composant2.N$377
  M1A: M1.A, IC3.1Y, Composant2.N$262
  M1C: M1.C, IC3.3Y, Composant2.N$251
  M1B: M1.B, IC3.2Y, Composant2.N$239
  M1D: M1.D, IC3.4Y, Composant2.N$272
  M2A: M2.A, IC4.1Y, Composant2.N$16
  M2C: M2.C, IC4.3Y, Composant2.N$383
  M2B: M2.B, IC4.2Y, Composant2.N$319
  M2D: M2.D, IC4.4Y, Composant2.N$39
  N1: IC3.1_2EN, IC3.3_4EN, IC4.1_2EN, IC4.3_4EN, Composant2.N$81, Composant2.N$165, Composant2.N$229, Composant2.N$276
  N2: Composant4.D3, Composant4.N$138, J2.pin2
  N3: Composant4.A4, Composant4.N$22, J4.pin7
  N4: Composant4.A3, Composant4.N$27, J4.pin2
  N5: Composant4.A2, Composant4.N$60, J3.pin2
  N6: Composant4.A1, Composant4.N$55, J3.pin7
  N7: Composant4.D11, Composant4.N$133, J2.pin7
  N8: Composant4.D12, Composant4.N$166, J1.pin7
  N9: Composant4.D13, Composant4.N$171, J1.pin2
  N10: Composant4.5V, Composant4.N$28, Composant4.N$129, J2.pin1, J4.pin1
  N11: Composant4.GND, Composant4.N$24, Composant4.N$25, Composant4.N$57, Composant4.N$58, Composant4.N$79, Composant4.N$124, Composant4.N$135, Composant4.N$136, Composant4.N$168, Composant4.N$169, J1.pin4, J1.pin5, J2.pin4, J2.pin5, J3.pin4, J3.pin5, J4.pin4, J4.pin5
  N12: Composant4.N$21, J4.pin8
  N13: Composant4.N$23, J4.pin6
  N14: Composant4.N$26, J4.pin3
  N15: Composant4.N$54, J3.pin8
  N16: Composant4.N$56, J3.pin6
  N17: Composant4.N$59, J3.pin3
  N18: Composant4.N$61, J3.pin1
  N19: Composant4.N$132, J2.pin8
  N20: Composant4.N$134, J2.pin6
  N21: Composant4.N$137, J2.pin3
  N22: Composant4.N$162, J1.pin1
  N23: Composant4.N$165, J1.pin8
  N24: Composant4.N$167, J1.pin6
  N25: Composant4.N$170, J1.pin3
